# Fritzing sketch circuit (saved by Fritzing 1.0.1rc)
breadboards: 1

parts:
  Raspberry_Pi_1 = Raspberry Pi 3 [part_number=RPI-3-V1.2]
  LED1 = LED - 5mm [color="Green (560nm)" current=0.030 package="5 mm [THT]"]
  LED2 = LED - 5mm [color="Red (633nm)" current=0.030 package="5 mm [THT]"]
  LED3 = LED - 5mm [color="Yellow (595nm)" current=0.030 package="5 mm [THT]"]
  R1 = Resistor [tolerance=±5% power=0.25 resistance=330 package=THT]
  R2 = Resistor [tolerance=±5% power=0.25 resistance=33 package=THT]
  R3 = Resistor [tolerance=±5% power=0.25 resistance=220 package=THT]

nets:
  N1: Raspberry_Pi_1.GPIO4, LED1.cathode
  N2: Raspberry_Pi_1.GND, R1.Pin_1, R2.Pin_1, R3.Pin_1
  N3: Raspberry_Pi_1.GPIO27, LED3.cathode
  N4: Raspberry_Pi_1.GPIO10, LED2.cathode
  N5: LED1.anode, R1.Pin_0
  N6: LED2.anode, R3.Pin_0
  N7: LED3.anode, R2.Pin_0
